// Logisim project Controlunit_jalrmissing.circ as structural Verilog
module Control_Unit (
  input  op2,
  input  op1,
  input  op0,
  output WD,
  output ALUSel1,
  output ALUSel0,
  output BSel,
  output PCSel,
  output WDSel1b,
  output WDSel0b,
  output MemoryRW
);

  wire and_2_out, and_3_out, and_6_out, and_7_out, and_8_out, and_9_out, and_10_out, and_12_out, and_13_out,
       not_1_out, not_2_out, not_3_out, not_4_out, not_5_out, not_6_out, not_7_out, not_8_out, not_9_out,
       not_10_out, not_11_out, not_12_out, not_13_out, not_14_out, not_15_out;

  not not_1 (not_1_out, op2);
  not not_2 (not_2_out, op1);
  not not_3 (not_3_out, op1);
  not not_4 (not_4_out, op1);
  not not_5 (not_5_out, op0);
  not not_6 (not_6_out, op2);
  not not_7 (not_7_out, op2);
  not not_8 (not_8_out, op0);
  not not_9 (not_9_out, op0);
  not not_10 (not_10_out, op2);
  not not_11 (not_11_out, op1);
  not not_12 (not_12_out, op0);
  not not_13 (not_13_out, op2);
  not not_14 (not_14_out, op1);
  and and_1 (WDSel0b, op2, op0);
  not not_15 (not_15_out, op0);
  and and_2 (and_2_out, not_1_out, not_2_out);
  and and_3 (and_3_out, not_3_out, op0);
  and and_4 (ALUSel1, op2, not_4_out, not_5_out);
  and and_5 (ALUSel0, not_6_out, op1);
  and and_6 (and_6_out, not_7_out, not_8_out);
  and and_7 (and_7_out, op1, not_9_out);
  and and_8 (and_8_out, op2, op0);
  and and_9 (and_9_out, not_10_out, op0);
  and and_10 (and_10_out, op2, not_11_out, not_12_out);
  and and_11 (WDSel1b, not_13_out, not_14_out, op0);
  and and_12 (and_12_out, op1, not_15_out);
  and and_13 (and_13_out, op2, op0);
  or or_1 (WD, and_2_out, and_3_out);
  or or_2 (BSel, and_6_out, and_7_out, and_8_out);
  or or_3 (PCSel, and_9_out, and_10_out);
  or or_4 (MemoryRW, and_12_out, and_13_out);
endmodule
